# Fritzing sketch Arduino_Collective (saved by Fritzing 0.9.3b)
breadboards: 1

parts:
  Part1 = Arduino Leonardo (Rev3b)
  R2 = Rotary Potentiometer (Large) [maximum_resistance=100kΩ package=THT]

nets:
  N1: Part1.5V, R2.leg1
  N2: Part1.GND, R2.leg2
  N3: Part1.A0, R2.wiper
